// Logisim project CPU16005.circ as structural Verilog: 8 circuits, main circuit main
// 1
module main (
);

  wire \Bildschirm_Löschen_out , bios_1_cpu_control, button_out, cpu_1_aus_d, cpu_1_aus_d_takt, cpu_1_aus_h,
       cpu_1_ein, cpu_1_steuerbus, Entf_out, Neustarten_out, pull_resistor_1_node, t_ff_1_q, Taktgeber_out,
       tastaturcontroller_1_hexdiesplaysteuerung, \zurücksetzen_out ;
  wire [3:0] cpu_1_displaysteuerung;
  wire [15:0] bios_1_boot_adressen, cpu_1_adressbus, cpu_1_datenbus_out, displaycontroller_1_out_6,
       displaycontroller_1_out_7, displaycontroller_1_out_8, displaycontroller_1_out_9,
       displaycontroller_1_out_10, displaycontroller_1_out_11, displaycontroller_1_out_12,
       displaycontroller_1_out_13, displaycontroller_1_out_14, displaycontroller_1_out_15,
       displaycontroller_1_out_16, displaycontroller_1_out_17, displaycontroller_1_out_18,
       displaycontroller_1_out_19, displaycontroller_1_out_20, displaycontroller_1_out_21, f_out,
       multiplexer_1_out, multiplexer_2_out, multiplexer_3_out, multiplexer_4_out, multiplexer_5_out,
       ram_1_data, register_1_q, rom_1_data, tastaturcontroller_1_out_4;

  DotMatrix #(.matrixcols(16), .matrixrows(16)) dotmatrix_1 (
    .col0(displaycontroller_1_out_6), .col1(displaycontroller_1_out_7), .col2(displaycontroller_1_out_8),
    .col3(displaycontroller_1_out_9), .col4(displaycontroller_1_out_10), .col5(displaycontroller_1_out_11),
    .col6(displaycontroller_1_out_12), .col7(displaycontroller_1_out_13), .col8(displaycontroller_1_out_14),
    .col9(displaycontroller_1_out_15), .col10(displaycontroller_1_out_16),
    .col11(displaycontroller_1_out_17), .col12(displaycontroller_1_out_18),
    .col13(displaycontroller_1_out_19), .col14(displaycontroller_1_out_20), .col15(displaycontroller_1_out_21));
  Displaycontroller displaycontroller_1 (
    .out_6(displaycontroller_1_out_6), .out_7(displaycontroller_1_out_7), .out_8(displaycontroller_1_out_8),
    .out_9(displaycontroller_1_out_9), .out_10(displaycontroller_1_out_10),
    .out_11(displaycontroller_1_out_11), .out_12(displaycontroller_1_out_12),
    .out_13(displaycontroller_1_out_13), .out_14(displaycontroller_1_out_14),
    .out_15(displaycontroller_1_out_15), .out_16(displaycontroller_1_out_16),
    .out_17(displaycontroller_1_out_17), .out_18(displaycontroller_1_out_18),
    .out_19(displaycontroller_1_out_19), .out_20(displaycontroller_1_out_20),
    .out_21(displaycontroller_1_out_21), .Displaysteuerung(cpu_1_displaysteuerung),
    .Ausgabe_Display(cpu_1_aus_d), .Displaydaten(cpu_1_datenbus_out), .\Löschen (\Bildschirm_Löschen_out ),
    .Ausgabe_Display_takt(cpu_1_aus_d_takt));
  Button \Bildschirm_Löschen  (.out(\Bildschirm_Löschen_out ));
  Pull_Resistor pull_resistor_1 (.node(pull_resistor_1_node));
  Transistor #(.gate("br")) transistor_1 (.in(Taktgeber_out), .out(pull_resistor_1_node), .gate(bios_1_cpu_control));
  Clock Taktgeber (.out(Taktgeber_out));
  Button \zurücksetzen  (.out(\zurücksetzen_out ));
  T_Flip_Flop t_ff_1 (
    .clk(cpu_1_aus_h), .T(cpu_1_aus_h), .Q(t_ff_1_q), .reset(tastaturcontroller_1_hexdiesplaysteuerung));  // open: Qn, preset, en
  Multiplexer #(.width(16), .disabled(0), .enable("false")) multiplexer_1 (
    .in0(tastaturcontroller_1_out_4), .in1(register_1_q), .out(multiplexer_1_out), .sel(t_ff_1_q));
  Register_part #(.width(16), .trigger("high")) register_1 (
    .D(cpu_1_datenbus_out), .Q(register_1_q), .clk(cpu_1_aus_h));  // open: en, clr
  CPU cpu_1 (
    .Datenbus_in(multiplexer_2_out), .Adressbus(cpu_1_adressbus), .Takt(pull_resistor_1_node),
    .Steuerbus(cpu_1_steuerbus), .Datenbus_out(cpu_1_datenbus_out), .\Löschen (\zurücksetzen_out ),
    .Ein(cpu_1_ein), .Aus_h(cpu_1_aus_h), .Best(button_out), .Aus_d(cpu_1_aus_d),
    .Displaysteuerung(cpu_1_displaysteuerung), .Aus_d_takt(cpu_1_aus_d_takt));
  Multiplexer #(.width(16), .disabled(0), .enable("false")) multiplexer_2 (
    .in0(ram_1_data), .in1(tastaturcontroller_1_out_4), .out(multiplexer_2_out), .sel(cpu_1_ein));
  LED \Lädt  (.in(bios_1_cpu_control));
  Hex_Digit_Display hex_digit_display_1 (.value(multiplexer_1_out[11:8]));  // open: dp
  Hex_Digit_Display hex_digit_display_2 (.value(multiplexer_1_out[15:12]));  // open: dp
  Hex_Digit_Display hex_digit_display_3 (.value(multiplexer_1_out[7:4]));  // open: dp
  Hex_Digit_Display hex_digit_display_4 (.value(multiplexer_1_out[3:0]));  // open: dp
  BIOS bios_1 (
    .Takt(Taktgeber_out), .cpu_control(bios_1_cpu_control), .boot_Adressen(bios_1_boot_adressen),
    .Neustarten(Neustarten_out));
  Button Neustarten (.out(Neustarten_out));
  LED Eingabe (.in(cpu_1_ein));
  Button e (.out(f_out[1]));
  Button d (.out(f_out[2]));
  Button a (.out(f_out[5]));
  Button b (.out(f_out[4]));
  Button _7 (.out(f_out[8]));
  Button _8 (.out(f_out[7]));
  Button _4 (.out(f_out[11]));
  Button _5 (.out(f_out[10]));
  Button _1 (.out(f_out[14]));
  Button _2 (.out(f_out[13]));
  Button _0 (.out(f_out[15]));
  Button Entf (.out(Entf_out));
  Button f (.out(f_out[0]));
  Button c (.out(f_out[3]));
  Button _9 (.out(f_out[6]));
  Button _6 (.out(f_out[9]));
  Button _3 (.out(f_out[12]));
  Button button (.out(button_out));
  Multiplexer #(.width(16), .disabled(0), .enable("false")) multiplexer_3 (
    .in0(cpu_1_adressbus), .in1(bios_1_boot_adressen), .out(multiplexer_3_out), .sel(bios_1_cpu_control));
  Multiplexer #(.width(16), .disabled(0), .enable("false")) multiplexer_4 (
    .in0(cpu_1_datenbus_out), .in1(ram_1_data), .out(multiplexer_4_out), .sel(cpu_1_steuerbus));
  ROM #(.addrWidth(16), .dataWidth(16)) rom_1 (.addr(bios_1_boot_adressen), .data(rom_1_data));  // open: sel
  Tastaturcontroller tastaturcontroller_1 (
    .T_Input(f_out), .\Löschen_automatisch (cpu_1_ein),
    .HexDiesplaySteuerung(tastaturcontroller_1_hexdiesplaysteuerung), .out_4(tastaturcontroller_1_out_4),
    .\Löschen_individuell (Entf_out));
  Multiplexer #(.width(16), .disabled(0), .enable("false")) multiplexer_5 (
    .in0(multiplexer_4_out), .in1(rom_1_data), .out(multiplexer_5_out), .sel(bios_1_cpu_control));
  RAM #(.addrWidth(16), .dataWidth(16), .bus("separate")) ram_1 (
    .addr(multiplexer_3_out), .din(multiplexer_5_out), .data(ram_1_data), .clk(Taktgeber_out),
    .ld(cpu_1_steuerbus), .clr(\zurücksetzen_out ));  // open: str, sel
  Pull_Resistor pull_resistor_2 (.node(ram_1_data));

  // Notes on the sheet:
  //   contents of rom_1 (hex, n*v repeats v):
  //   0 200 d0 2200 200 d1 2201 200 d2 2202 200 d3 2203 200 d4 2204 200 d5 2205 200 d6 2206 200 d7 2207
  //   200 d8 2208 200 d9 2209 200 da 220a 200 db 220b 200 dc 220c 200 dd 220d 200 de 220e 200 df 220f 1e00
  //   1800 157*0 f3bc a534 43a4 0 f780 a4bc 5300 0 f7bc 9510 f29c 0 f03c 9024 300c 33*0 204 1d0 2300 204
  //   1d1 2301 204 1d2 2302 204 1d3 2303 204 1d4 2304 204 1d5 2305 204 1d6 2306 204 1d7 2307 204 1d8 2308
  //   204 1d9 2309 204 1da 230a 204 1db 230b 204 1dc 230c 204 1dd 230d 204 1de 230e 0 0 0 1e00 204 1e0
  //   2300 204 1e1 2301 204 1e2 2302 204 1e3 2303 204 1e4 2304 204 1e5 2305 204 1e6 2306 204 1e7 2307 204
  //   1e8 2308 204 1e9 2309 204 1ea 230a 204 1eb 230b 204 1ec 230c 204 1ed 230d 204 1ee 230e 0 0 1e01 204
  //   1f0 2300 204 1f1 2301 204 1f2 2302 204 1f3 2303 204 1f4 2304 204 1f5 2305 204 1f6 2306 204 1f7 2307
  //   204 1f8 2308 204 1f9 2309 204 1fa 230a 204 1fb 230b 204 1fc 230c 204 1fd 230d 204 1fe 230e 0 0 1e02
  //   204 1c0 205 1c1 206 1c2 207 1c3 1708 1a28 1024 9ad 1838 883 2018 207 1c4 1838 a83 2018 207 1c4 1838
  //   c83 2018 207 1c4 1838 e83 2018 207 1c4 1838 14*0 a 19e 5 199 12*0 f780 680 1480 0 f000 9780 f000 0
  //   f780 a200 4380 0 780 480 180 0 f780 9680 f480 0 f000 a780 4000 0 780 200 380 0 780 480 180 0 b780
  //   b680 d480 0 f000 9780 f000 0 f780 a200 4380 0 780 480 180 0 200 240 2200 200 241 2201 200 242 2202
  //   200 243 2203 200 244 2204 200 245 2205 200 246 2206 200 247 2207 200 248 2208 200 249 2209 200 24a
  //   220a 200 24b 220b 200 24b 220c 200 24b 220d 200 24b 220e 200 24b 220f 200 24b 201 24c 202 24d 1000
  //   2440 1c10 200 24e 1800 4*0 8420 f7bc 8420 0 3bc f524 3bc 0 f7bc 94b4 94a4 0 1a0 236 260 17*0 200 2a0
  //   201 2a1 2200 2241 2242 2243 2244 2205 2246 2247 2248 2249 220a 224b 224c 224d 224e 220f 400 320 400
  //   325 400 32a 400 32f 408 321 408 322 408 323 408 324 408 326 408 327 408 328 408 329 408 32b 408 32c
  //   408 32d 408 32e 200 2a2 1800 9*0 ffff 8421 2c0 29*0 201 2e8 202 2e9 203 2ea 204 2eb 205 2ec 206 2ef
  //   2030 1e00 2440 1680 1a18 0 906 430 2d6 207 0 27d0 1a18 976 430 2dd 207 0 27d0 1a18 201 2ed 202 2ee
  //   c40 880 1800 0 9 0 2ca 300 10 30 310 1111 80*0 200 321 201 322 202 360 203 361 880 8c9 0 0 400 321
  //   400 324 408 322 408 323 2201 2204 2242 2243 200 362 400 301 200 363 1800 0 c 12 1 50c 12*0 200 326
  //   201 327 202 390 203 391 880 8c9 0 0 400 326 400 329 408 327 408 328 2206 2209 2247 2248 200 392 400
  //   302 200 393 1800 0 c 12 1 50c 12*0 200 32b 201 32c 202 3c0 203 3c1 880 8c9 0 0 400 32b 400 32e 408
  //   32c 408 32d 220b 220e 224c 224d 200 3c2 400 303 200 3c3 1800 0 c 12 1 50c 12*0 200 321 201 322 202
  //   3f0 203 3f1 880 8c9 0 0 400 321 400 324 408 322 408 323 2201 2204 2242 2243 200 3f2 400 304 200 3f3
  //   1800 0 180 240 1 50c 12*0 200 326 201 327 202 420 203 421 880 8c9 0 0 400 326 400 329 408 327 408
  //   328 2206 2209 2247 2248 200 422 400 305 200 423 1800 0 180 240 1 50c 12*0 200 32b 201 32c 202 450
  //   203 451 880 8c9 0 0 400 32b 400 32e 408 32c 408 32d 220b 220e 224c 224d 200 452 400 306 200 453 1800
  //   0 180 240 1 50c 12*0 200 321 201 322 202 480 203 481 880 8c9 0 0 400 321 400 324 408 322 408 323
  //   2201 2204 2242 2243 200 482 400 307 200 483 1800 0 3000 4800 1 50c 12*0 200 326 201 327 202 4b0 203
  //   4b1 880 8c9 0 0 400 326 400 329 408 327 408 328 2206 2209 2247 2248 200 4b2 400 308 200 4b3 1800 0
  //   3000 4800 1 50c 12*0 200 32b 201 32c 202 4e0 203 4e1 880 8c9 0 0 400 32b 400 32e 408 32c 408 32d
  //   220b 220e 224c 224d 200 4e2 400 309 200 4e3 1800 0 3000 4800 1 50c 40*0 204 5b4 205 5b5 200 301 201
  //   302 202 303 203 5b8 1700 1a18 1708 1a18 1710 1a18 1828 0 200 304 201 305 202 306 203 5b9 1700 1a18
  //   1708 1a18 1710 1a18 1828 0 200 307 201 308 202 309 203 5ba 1700 1a18 1708 1a18 1710 1a18 1828 0 200
  //   301 201 304 202 307 203 5bb 1700 1a18 1708 1a18 1710 1a18 1828 0 200 302 201 305 202 308 203 5bc
  //   1700 1a18 1708 1a18 1710 1a18 1828 0 200 303 201 306 202 309 203 5bd 1700 1a18 1708 1a18 1710 1a18
  //   1828 0 200 301 201 305 202 309 203 5be 1700 1a18 1708 1a18 1710 1a18 1828 0 200 303 201 305 202 307
  //   203 5bf 1700 1a18 1708 1a18 1710 1a18 1828 0 200 5aa 202 5ab 203 5ac 204 5ad 205 5ae 206 5af 410 59f
  //   201 0 840 1012 26d0 1a30 2500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
endmodule

module Register (
  input  [2:0] Ziel,
  input  Lade,
  input  [15:0] Operant_in,
  input  Takt,
  input  \Löschen ,
  input  \Fl_lö ,
  input  kein_Registertakt,
  input  [1:0] Vergleiche,
  input  [2:0] Quelle_1,
  input  [2:0] Quelle_2,
  input  Sende,
  input  Aus_d,
  input  [2:0] Operationssteuerung,
  output Flag,
  output [15:0] Operant_out
);

  wire alu_1_flag_in, decoder_1_out0, decoder_1_out1, decoder_1_out2, decoder_1_out3, decoder_1_out4,
       decoder_1_out5, decoder_1_out6, decoder_1_out7, or_1_out, or_2_out, pull_resistor_1_node,
       transistor_2_out;
  wire [15:0] alu_1_alu_ergebnis_zu_registern, multiplexer_1_out, multiplexer_2_out, multiplexer_3_out,
       multiplexer_4_out, R0_q, R1_q, R2_q, R3_q, R4_q, R5_q, R6_q, R7_q;

  Pull_Resistor pull_resistor_1 (.node(pull_resistor_1_node));
  Transistor #(.gate("br")) transistor_1 (.in(Takt), .out(pull_resistor_1_node), .gate(kein_Registertakt));
  Register_part #(.width(16)) R0 (
    .D(multiplexer_4_out), .en(decoder_1_out0), .Q(R0_q), .clk(pull_resistor_1_node), .clr(\Löschen ));
  Register_part #(.width(16)) R1 (
    .D(multiplexer_4_out), .en(decoder_1_out1), .Q(R1_q), .clk(pull_resistor_1_node), .clr(\Löschen ));
  Register_part #(.width(16)) R2 (
    .D(multiplexer_4_out), .en(decoder_1_out2), .Q(R2_q), .clk(pull_resistor_1_node), .clr(\Löschen ));
  Decoder #(.select(3), .disabled(0), .enable("false")) decoder_1 (
    .out0(decoder_1_out0), .out1(decoder_1_out1), .out2(decoder_1_out2), .out3(decoder_1_out3),
    .out4(decoder_1_out4), .out5(decoder_1_out5), .out6(decoder_1_out6), .out7(decoder_1_out7), .sel(Ziel));
  Multiplexer #(.select(3), .width(16), .disabled(0), .enable("false")) multiplexer_1 (
    .in0(R0_q), .in1(R1_q), .in2(R2_q), .in3(R3_q), .in4(R4_q), .in5(R5_q), .in6(R6_q), .in7(R7_q),
    .out(multiplexer_1_out), .sel(Quelle_1));
  Register_part #(.width(16)) R3 (
    .D(multiplexer_4_out), .en(decoder_1_out3), .Q(R3_q), .clk(pull_resistor_1_node), .clr(\Löschen ));
  ALU alu_1 (
    .Operator_1_von_Registern(multiplexer_1_out), .Operator_2_von_Registern(multiplexer_2_out),
    .Operationssteuerung(Operationssteuerung), .ALU_Ergebnis_zu_Registern(alu_1_alu_ergebnis_zu_registern),
    .Flag_In(alu_1_flag_in), .Vergleiche(Vergleiche));
  Register_part #(.width(16)) R4 (
    .D(multiplexer_4_out), .en(decoder_1_out4), .Q(R4_q), .clk(pull_resistor_1_node), .clr(\Löschen ));
  Register_part #(.width(16)) R5 (
    .D(multiplexer_4_out), .en(decoder_1_out5), .Q(R5_q), .clk(pull_resistor_1_node), .clr(\Löschen ));
  Multiplexer #(.select(3), .width(16), .disabled(0), .enable("false")) multiplexer_2 (
    .in0(R0_q), .in1(R1_q), .in2(R2_q), .in3(R3_q), .in4(R4_q), .in5(R5_q), .in6(R6_q), .in7(R7_q),
    .out(multiplexer_2_out), .sel(Quelle_2));
  Register_part #(.width(16)) R6 (
    .D(multiplexer_4_out), .en(decoder_1_out6), .Q(R6_q), .clk(pull_resistor_1_node), .clr(\Löschen ));
  Multiplexer #(.width(16), .disabled(0), .enable("false")) multiplexer_3 (
    .in0(multiplexer_1_out), .in1(multiplexer_2_out), .out(multiplexer_3_out), .sel(Aus_d));
  Register_part #(.width(16)) R7 (
    .D(multiplexer_4_out), .en(decoder_1_out7), .Q(R7_q), .clk(pull_resistor_1_node), .clr(\Löschen ));
  Multiplexer #(.width(16), .disabled(0), .enable("false")) multiplexer_4 (
    .in0(alu_1_alu_ergebnis_zu_registern), .in1(Operant_in), .out(multiplexer_4_out), .sel(Lade));
  Transistor #(.\type ("n"), .gate("br")) transistor_2 (.in(Takt), .out(transistor_2_out), .gate(or_1_out));
  Pull_Resistor pull_resistor_2 (.node(transistor_2_out));
  or or_1 (or_1_out, Vergleiche[1], Vergleiche[0]);
  Transistor #(.\type ("n"), .width(16)) transistor_3 (.in(multiplexer_3_out), .out(Operant_out), .gate(Sende));
  Pull_Resistor pull_resistor_3 (.node(Operant_out));
  D_Flip_Flop u_Flag (.clk(transistor_2_out), .D(alu_1_flag_in), .Q(Flag), .reset(or_2_out));  // open: Qn, preset, en
  or or_2 (or_2_out, \Löschen , \Fl_lö );
endmodule

module ALU (
  input  [15:0] Operator_1_von_Registern,
  input  [15:0] Operator_2_von_Registern,
  input  [2:0] Operationssteuerung,
  input  [1:0] Vergleiche,
  output [15:0] ALU_Ergebnis_zu_Registern,
  output Flag_In
);

  wire comparator_1_eq, comparator_1_gt, comparator_1_lt;
  wire [15:0] adder_1_out, adder_2_out, divider_1_out, multiplier_1_out, negator_1_out, subtractor_1_out,
       subtractor_2_out;

  Adder #(.width(16)) adder_1 (
    .a(Operator_1_von_Registern), .b(Operator_2_von_Registern), .out(adder_1_out));  // open: cin, cout
  Subtractor #(.width(16)) subtractor_1 (
    .a(Operator_1_von_Registern), .b(Operator_2_von_Registern), .out(subtractor_1_out));  // open: bin, bout
  Multiplier #(.width(16)) multiplier_1 (
    .a(Operator_1_von_Registern), .b(Operator_2_von_Registern), .out(multiplier_1_out));  // open: cin, cout
  Divider #(.width(16)) divider_1 (
    .a(Operator_1_von_Registern), .b(Operator_2_von_Registern), .out(divider_1_out));  // open: upper, rem
  Adder #(.width(16)) adder_2 (.a(Operator_1_von_Registern), .b(16'h1), .out(adder_2_out));  // open: cin, cout
  Subtractor #(.width(16)) subtractor_2 (
    .a(Operator_1_von_Registern), .b(16'h1), .out(subtractor_2_out));  // open: bin, bout
  Negator #(.width(16)) negator_1 (.in(Operator_1_von_Registern), .out(negator_1_out));
  Comparator #(.width(16), .mode("unsigned")) comparator_1 (
    .a(Operator_1_von_Registern), .b(Operator_2_von_Registern), .gt(comparator_1_gt), .eq(comparator_1_eq),
    .lt(comparator_1_lt));
  Multiplexer #(.select(2), .disabled(0), .enable("false")) multiplexer_1 (
    .in1(comparator_1_eq), .in2(comparator_1_gt), .in3(comparator_1_lt), .out(Flag_In), .sel(Vergleiche));  // open: in0
  Pull_Resistor pull_resistor_1 (.node(Flag_In));
  Multiplexer #(.select(3), .width(16), .disabled(0), .enable("false")) multiplexer_2 (
    .in0(Operator_1_von_Registern), .in1(adder_1_out), .in2(subtractor_1_out), .in3(multiplier_1_out),
    .in4(divider_1_out), .in5(adder_2_out), .in6(subtractor_2_out), .in7(negator_1_out),
    .out(ALU_Ergebnis_zu_Registern), .sel(Operationssteuerung));
  Pull_Resistor pull_resistor_2 (.node(ALU_Ergebnis_zu_Registern));

  // Notes on the sheet:
  //   Bewege
endmodule

module CPU (
  input  [15:0] Datenbus_in,
  input  Best,
  input  Takt,
  input  \Löschen ,
  output [15:0] Datenbus_out,
  output Steuerbus,
  output Ein,
  output [15:0] Adressbus,
  output Aus_h,
  output Aus_d,
  output Aus_d_takt,
  output [3:0] Displaysteuerung
);

  wire register_1_flag, \steuerwerk_1_fl_lö , steuerwerk_1_kein_registertakt_2, steuerwerk_1_lade,
       steuerwerk_1_sende;
  wire [1:0] steuerwerk_1_vergleiche;
  wire [2:0] steuerwerk_1_operationssteuerung, \steuerwerk_1_quelle_1_für_register ,
       \steuerwerk_1_quelle_2_für_register , \steuerwerk_1_ziel_für_register ;
  wire [15:0] steuerwerk_1_operant_zu_register;

  Steuerwerk steuerwerk_1 (
    .Datenbus(Datenbus_in), .Takt(Takt), .\Takt_für_Register_2___5 (Aus_d_takt),
    .\Ziel_für_Register (\steuerwerk_1_ziel_für_register ),
    .\Quelle_1_für_Register (\steuerwerk_1_quelle_1_für_register ),
    .\Quelle_2_für_Register (\steuerwerk_1_quelle_2_für_register ), .Adressbus(Adressbus),
    .Operant_zu_Register(steuerwerk_1_operant_zu_register),
    .Operationssteuerung(steuerwerk_1_operationssteuerung), .Lade(steuerwerk_1_lade), .Steuerbus(Steuerbus),
    .Sende(steuerwerk_1_sende), .\Löschen (\Löschen ), .Flag(register_1_flag),
    .Vergleiche(steuerwerk_1_vergleiche), .kein_Registertakt_2(steuerwerk_1_kein_registertakt_2),
    .Datenbus_Register(Datenbus_out), .Eingabe(Ein), .Ausgabe_hex(Aus_h), .\Bestätigt (Best),
    .\Fl_lö (\steuerwerk_1_fl_lö ), .Ausgabe_Display(Aus_d), .Displaysteuerung(Displaysteuerung));
  Register register_1 (
    .Quelle_1(\steuerwerk_1_quelle_1_für_register ), .Quelle_2(\steuerwerk_1_quelle_2_für_register ),
    .Operationssteuerung(steuerwerk_1_operationssteuerung), .Ziel(\steuerwerk_1_ziel_für_register ),
    .Takt(Aus_d_takt), .Operant_in(steuerwerk_1_operant_zu_register), .Lade(steuerwerk_1_lade),
    .Operant_out(Datenbus_out), .Sende(steuerwerk_1_sende), .\Löschen (\Löschen ), .Flag(register_1_flag),
    .Vergleiche(steuerwerk_1_vergleiche), .kein_Registertakt(steuerwerk_1_kein_registertakt_2),
    .\Fl_lö (\steuerwerk_1_fl_lö ), .Aus_d(Aus_d));

  // Notes on the sheet:
  //   Steuerwerk
  //   Register
endmodule

module Steuerwerk (
  input  [15:0] Datenbus,
  input  Flag,
  input  [15:0] Datenbus_Register,
  input  \Löschen ,
  input  \Bestätigt ,
  input  Takt,
  output \Takt_für_Register_2___5 ,
  output kein_Registertakt_2,
  output [15:0] Operant_zu_Register,
  output [3:0] Displaysteuerung,
  output [2:0] \Ziel_für_Register ,
  output [2:0] \Quelle_1_für_Register ,
  output Lade,
  output [2:0] \Quelle_2_für_Register ,
  output Sende,
  output \Fl_lö ,
  output [2:0] Operationssteuerung,
  output Eingabe,
  output Ausgabe_hex,
  output [1:0] Vergleiche,
  output Ausgabe_Display,
  output Steuerbus,
  output [15:0] Adressbus
);

  wire comparator_1_eq, d_ff_1_q, decoder_1_out0, decoder_1_out1, decoder_1_out2, decoder_1_out3,
       decoder_1_out4, decoder_1_out5, decoder_2_out0, decoder_2_out1, decoder_2_out2, decoder_2_out3,
       decoder_2_out4, decoder_2_out5, decoder_2_out6, decoder_2_out7, decoder_2_out8, decoder_2_out9,
       decoder_2_out10, decoder_2_out11, decoder_2_out13, decoder_2_out14, decoder_2_out18, decoder_2_out19,
       or_1_out, or_2_out, or_4_out, or_5_out, or_6_out, or_7_out, or_8_out, or_9_out, or_10_out, or_12_out,
       or_13_out, or_14_out, or_15_out, or_16_out, pull_resistor_3_node, pull_resistor_5_node,
       pull_resistor_6_node, pull_resistor_8_node, Stop_q, transistor_2_out, transistor_4_out,
       transistor_6_out, transistor_9_out, transistor_10_out, transistor_11_out;
  wire [2:0] Taktteiler_q, transistor_1_out;
  wire [15:0] adder_1_out, BZ_q, DR_q, multiplexer_1_out, multiplexer_2_out;
  wire [15:9] BR_q;

  Transistor #(.width(3)) transistor_1 (.in(Taktteiler_q), .out(transistor_1_out), .gate(or_1_out));
  Pull_Resistor pull_resistor_1 (.node(transistor_1_out));
  Comparator #(.width(3), .mode("unsigned")) comparator_1 (
    .a(transistor_1_out), .b(3'b011), .eq(comparator_1_eq));  // open: gt, lt
  or or_1 (or_1_out, decoder_2_out1, decoder_2_out2);
  Counter #(.width(3), .max('h5)) Taktteiler (
    .Q(Taktteiler_q), .clk(transistor_2_out), .clr(or_2_out));  // open: load, D, count, carry
  or or_2 (or_2_out, \Löschen , comparator_1_eq);
  or or_3 (\Takt_für_Register_2___5 , decoder_1_out5, decoder_1_out2);
  Decoder #(.select(3), .disabled(0), .enable("false")) decoder_1 (
    .out0(decoder_1_out0), .out1(decoder_1_out1), .out2(decoder_1_out2), .out3(decoder_1_out3),
    .out4(decoder_1_out4), .out5(decoder_1_out5), .sel(Taktteiler_q));  // open: out6, out7
  Transistor transistor_2 (.in(Takt), .out(transistor_2_out), .gate(Stop_q));
  Pull_Resistor pull_resistor_2 (.node(transistor_2_out));
  or or_4 (or_4_out, pull_resistor_3_node, \Löschen );
  Pull_Resistor pull_resistor_3 (.node(pull_resistor_3_node));
  Transistor #(.\type ("n")) transistor_3 (.in(decoder_1_out0), .out(pull_resistor_3_node), .gate(Eingabe));
  Register_part #(.width(16)) BR (
    .D(Datenbus), .Q({BR_q, \Quelle_2_für_Register , \Quelle_1_für_Register [2:1], Displaysteuerung}),
    .clk(decoder_1_out1), .clr(or_4_out));  // open: en
  Register_part #(.width(16)) DR (.D(Datenbus), .Q(DR_q), .clk(decoder_1_out3), .clr(\Löschen ));  // open: en
  D_Flip_Flop Stop (.clk(Eingabe), .D(Eingabe), .Q(Stop_q), .reset(or_5_out));  // open: Qn, preset, en
  or or_5 (or_5_out, \Löschen , d_ff_1_q);
  Adder #(.width(16)) adder_1 (.a(BZ_q), .b(16'h1), .out(adder_1_out));  // open: cin, cout
  Transistor #(.\type ("n")) transistor_4 (.in(decoder_1_out2), .out(transistor_4_out), .gate(or_6_out));
  Pull_Resistor pull_resistor_4 (.node(transistor_4_out));
  Pull_Resistor pull_resistor_5 (.node(pull_resistor_5_node));
  or or_6 (or_6_out, pull_resistor_5_node, transistor_6_out, pull_resistor_8_node);
  Pull_Resistor pull_resistor_6 (.node(pull_resistor_6_node));
  Transistor #(.\type ("n"), .gate("br")) transistor_5 (.in(or_6_out), .out(pull_resistor_6_node), .gate(or_8_out));
  Multiplexer #(.width(16), .disabled(0), .enable("false")) multiplexer_1 (
    .in0(adder_1_out), .in1(Datenbus_Register), .out(multiplexer_1_out), .sel(pull_resistor_6_node));
  Register_part #(.width(16)) BZ (.D(multiplexer_1_out), .Q(BZ_q), .clk(or_7_out), .clr(\Löschen ));  // open: en
  or or_7 (or_7_out, transistor_4_out, decoder_1_out1, decoder_1_out4);
  D_Flip_Flop #(.trigger("falling")) d_ff_1 (
    .clk(\Bestätigt ), .D(1'b1), .Q(d_ff_1_q), .reset(d_ff_1_q));  // open: Qn, preset, en
  Transistor #(.\type ("n")) transistor_6 (.in(decoder_2_out13), .out(transistor_6_out), .gate(Flag));
  Pull_Resistor pull_resistor_7 (.node(transistor_6_out));
  Pull_Resistor pull_resistor_8 (.node(pull_resistor_8_node));
  Transistor transistor_7 (.in(decoder_2_out14), .out(pull_resistor_8_node), .gate(Flag));
  or or_8 (or_8_out, decoder_1_out1, decoder_1_out2);
  Decoder #(.select(5), .tristate("true"), .disabled(0), .enable("false")) decoder_2 (
    .out0(decoder_2_out0), .out1(decoder_2_out1), .out2(decoder_2_out2), .out3(decoder_2_out3),
    .out4(decoder_2_out4), .out5(decoder_2_out5), .out6(decoder_2_out6), .out7(decoder_2_out7),
    .out8(decoder_2_out8), .out9(decoder_2_out9), .out10(decoder_2_out10), .out11(decoder_2_out11),
    .out12(pull_resistor_5_node), .out13(decoder_2_out13), .out14(decoder_2_out14), .out15(Eingabe),
    .out16(Ausgabe_hex), .out17(Ausgabe_Display), .out18(decoder_2_out18), .out19(decoder_2_out19),
    .sel(BR_q[13:9]));  // open: out20, out21, out22, out23, out24, out25, out26, out27, out28, out29, out30, out31
  Pull_Resistor pull_resistor_9 (.node(decoder_2_out0));
  Pull_Resistor pull_resistor_10 (.node(decoder_2_out1));
  Pull_Resistor pull_resistor_11 (.node(decoder_2_out2));
  Pull_Resistor pull_resistor_12 (.node(decoder_2_out3));
  Pull_Resistor pull_resistor_13 (.node(\Fl_lö ));
  Transistor #(.\type ("n"), .gate("br")) transistor_8 (.in(or_9_out), .out(\Fl_lö ), .gate(decoder_1_out0));
  or or_9 (or_9_out, pull_resistor_5_node, decoder_2_out13, decoder_2_out14);
  Pull_Resistor pull_resistor_14 (.node(decoder_2_out4));
  Pull_Resistor pull_resistor_15 (.node(decoder_2_out5));
  Pull_Resistor pull_resistor_16 (.node(decoder_2_out6));
  Pull_Resistor pull_resistor_17 (.node(Eingabe));
  Pull_Resistor pull_resistor_18 (.node(Ausgabe_hex));
  Pull_Resistor pull_resistor_19 (.node(Ausgabe_Display));
  Multiplexer #(.width(16), .disabled(0), .enable("false")) multiplexer_2 (
    .in0(BZ_q), .in1(DR_q), .out(multiplexer_2_out), .sel(transistor_9_out));
  Transistor #(.\type ("n")) transistor_9 (.in(or_10_out), .out(transistor_9_out), .gate(or_1_out));
  Pull_Resistor pull_resistor_20 (.node(transistor_9_out));
  or or_10 (or_10_out, decoder_1_out3, decoder_1_out4);
  or or_11 (kein_Registertakt_2, transistor_10_out, decoder_2_out2);
  Pull_Resistor pull_resistor_21 (.node(decoder_2_out7));
  Pull_Resistor pull_resistor_22 (.node(decoder_2_out8));
  Pull_Resistor pull_resistor_23 (.node(decoder_2_out9));
  Pull_Resistor pull_resistor_24 (.node(decoder_2_out10));
  Pull_Resistor pull_resistor_25 (.node(decoder_2_out11));
  Pull_Resistor pull_resistor_26 (.node(pull_resistor_5_node));
  Pull_Resistor pull_resistor_27 (.node(decoder_2_out13));
  Pull_Resistor pull_resistor_28 (.node(decoder_2_out14));
  or or_12 (or_12_out, Ausgabe_hex, Ausgabe_Display);
  Register_part #(.width(16)) AR (.D(multiplexer_2_out), .Q(Adressbus), .clk(or_13_out), .clr(\Löschen ));  // open: en
  or or_13 (or_13_out, decoder_1_out0, decoder_1_out2, decoder_1_out4);
  Transistor #(.\type ("n"), .gate("br")) transistor_10 (.in(or_14_out), .out(transistor_10_out), .gate(or_16_out));
  Pull_Resistor pull_resistor_29 (.node(transistor_10_out));
  or or_14 (or_14_out, decoder_2_out0, decoder_2_out1, decoder_2_out2, decoder_2_out2, or_15_out, pull_resistor_5_node, decoder_2_out13, decoder_2_out14, or_12_out);
  or or_15 (or_15_out, decoder_2_out11, decoder_2_out19, decoder_2_out19);
  Pull_Resistor pull_resistor_30 (.node(decoder_2_out19));
  Transistor #(.\type ("n")) transistor_11 (.in(decoder_2_out2), .out(transistor_11_out), .gate(decoder_1_out5));
  Pull_Resistor pull_resistor_31 (.node(transistor_11_out));
  Pull_Resistor pull_resistor_32 (.node(Steuerbus));
  Transistor transistor_12 (.in(1'b1), .out(Steuerbus), .gate(transistor_11_out));
  or or_16 (or_16_out, decoder_1_out1, decoder_1_out2);
  or or_17 (Lade, decoder_2_out1, Eingabe);
  or or_18 (Vergleiche[0], decoder_2_out11, decoder_2_out19);
  or or_19 (Vergleiche[1], decoder_2_out19, decoder_2_out18);
  Pull_Resistor pull_resistor_33 (.node(decoder_2_out18));
  or or_20 (Sende, pull_resistor_5_node, decoder_2_out13, decoder_2_out14, decoder_2_out2, or_12_out);
  or or_21 (Operationssteuerung[0], decoder_2_out4, decoder_2_out6, decoder_2_out8, decoder_2_out10);
  or or_22 (Operationssteuerung[1], decoder_2_out5, decoder_2_out6, decoder_2_out9, decoder_2_out10);
  or or_23 (Operationssteuerung[2], decoder_2_out7, decoder_2_out8, decoder_2_out9, decoder_2_out10);

  assign Operant_zu_Register = Datenbus;
  assign \Quelle_1_für_Register [0] = Displaysteuerung[3];
  assign \Ziel_für_Register  = Displaysteuerung[2:0];

  // Notes on the sheet:
  //   OPcode
  //   Reserve
endmodule

module BIOS (
  input  Neustarten,
  input  Takt,
  output [15:0] boot_Adressen,
  output cpu_control
);

  wire comparator_1_gt, pull_resistor_2_node;

  D_Flip_Flop d_ff_1 (
    .clk(comparator_1_gt), .D(comparator_1_gt), .Qn(cpu_control), .reset(Neustarten));  // open: Q, preset, en
  Pull_Resistor pull_resistor_1 (.node(cpu_control));
  Pull_Resistor pull_resistor_2 (.node(pull_resistor_2_node));
  Transistor #(.\type ("n")) transistor_1 (.in(Takt), .out(pull_resistor_2_node), .gate(cpu_control));
  Comparator #(.width(16), .mode("unsigned")) comparator_1 (
    .a(boot_Adressen), .b(16'hbff), .gt(comparator_1_gt));  // open: eq, lt
  Counter #(.width(16), .max('hffff)) \Zähler  (
    .Q(boot_Adressen), .clk(pull_resistor_2_node), .clr(Neustarten));  // open: load, D, count, carry
  Pull_Resistor pull_resistor_3 (.node(boot_Adressen));
endmodule

module Tastaturcontroller (
  input  [15:0] T_Input,
  input  \Löschen_automatisch ,
  input  \Löschen_individuell ,
  output [15:0] out_4,
  output HexDiesplaySteuerung
);

  wire d_ff_1_q, or_2_out;
  wire [15:0] adder_1_out, adder_2_out, or_1_out, pull_resistor_2_node, pull_resistor_3_node,
       pull_resistor_5_node, pull_resistor_7_node, pull_resistor_8_node, pull_resistor_9_node,
       pull_resistor_11_node, pull_resistor_13_node, pull_resistor_15_node, shift_register_1_q0,
       shift_register_1_q1, shift_register_1_q2, shift_register_1_q3, shifter_1_out, shifter_2_out,
       shifter_3_out, transistor_1_out, transistor_4_out, transistor_6_out, transistor_10_out,
       transistor_12_out, transistor_14_out, transistor_16_out;

  Comparator #(.width(16), .mode("unsigned")) comparator_1 (
    .a(T_Input), .b({16{1'b0}}), .gt(HexDiesplaySteuerung));  // open: eq, lt
  Transistor #(.\type ("n"), .width(16)) transistor_1 (.in(16'hf), .out(transistor_1_out), .gate(T_Input[0]));
  Pull_Resistor pull_resistor_1 (.node(transistor_1_out));
  Pull_Resistor pull_resistor_2 (.node(pull_resistor_2_node));
  Transistor #(.\type ("n"), .width(16)) transistor_2 (.in(16'he), .out(pull_resistor_2_node), .gate(T_Input[1]));
  Pull_Resistor pull_resistor_3 (.node(pull_resistor_3_node));
  Transistor #(.\type ("n"), .width(16)) transistor_3 (.in(16'hd), .out(pull_resistor_3_node), .gate(T_Input[2]));
  Transistor #(.\type ("n"), .width(16)) transistor_4 (.in(16'hc), .out(transistor_4_out), .gate(T_Input[3]));
  Pull_Resistor pull_resistor_4 (.node(transistor_4_out));
  Pull_Resistor pull_resistor_5 (.node(pull_resistor_5_node));
  Transistor #(.\type ("n"), .width(16)) transistor_5 (.in(16'hb), .out(pull_resistor_5_node), .gate(T_Input[4]));
  Transistor #(.\type ("n"), .width(16)) transistor_6 (.in(16'ha), .out(transistor_6_out), .gate(T_Input[5]));
  Pull_Resistor pull_resistor_6 (.node(transistor_6_out));
  Pull_Resistor pull_resistor_7 (.node(pull_resistor_7_node));
  Transistor #(.\type ("n"), .width(16)) transistor_7 (.in(16'h9), .out(pull_resistor_7_node), .gate(T_Input[6]));
  Pull_Resistor pull_resistor_8 (.node(pull_resistor_8_node));
  Transistor #(.\type ("n"), .width(16)) transistor_8 (.in(16'h8), .out(pull_resistor_8_node), .gate(T_Input[7]));
  Pull_Resistor pull_resistor_9 (.node(pull_resistor_9_node));
  Transistor #(.\type ("n"), .width(16)) transistor_9 (.in(16'h7), .out(pull_resistor_9_node), .gate(T_Input[8]));
  Transistor #(.\type ("n"), .width(16)) transistor_10 (.in(16'h6), .out(transistor_10_out), .gate(T_Input[9]));
  Pull_Resistor pull_resistor_10 (.node(transistor_10_out));
  Pull_Resistor pull_resistor_11 (.node(pull_resistor_11_node));
  Transistor #(.\type ("n"), .width(16)) transistor_11 (.in(16'h5), .out(pull_resistor_11_node), .gate(T_Input[10]));
  Transistor #(.\type ("n"), .width(16)) transistor_12 (.in(16'h4), .out(transistor_12_out), .gate(T_Input[11]));
  Pull_Resistor pull_resistor_12 (.node(transistor_12_out));
  Pull_Resistor pull_resistor_13 (.node(pull_resistor_13_node));
  Transistor #(.\type ("n"), .width(16)) transistor_13 (.in(16'h3), .out(pull_resistor_13_node), .gate(T_Input[12]));
  Transistor #(.\type ("n"), .width(16)) transistor_14 (.in(16'h2), .out(transistor_14_out), .gate(T_Input[13]));
  Pull_Resistor pull_resistor_14 (.node(transistor_14_out));
  Pull_Resistor pull_resistor_15 (.node(pull_resistor_15_node));
  Transistor #(.\type ("n"), .width(16)) transistor_15 (.in(16'h1), .out(pull_resistor_15_node), .gate(T_Input[14]));
  Transistor #(.\type ("n"), .width(16)) transistor_16 (.in({16{1'b0}}), .out(transistor_16_out), .gate(T_Input[15]));
  Pull_Resistor pull_resistor_16 (.node(transistor_16_out));
  assign or_1_out = transistor_1_out | pull_resistor_2_node | pull_resistor_3_node | transistor_4_out | pull_resistor_5_node | transistor_6_out | pull_resistor_7_node | pull_resistor_8_node | pull_resistor_9_node | transistor_10_out | pull_resistor_11_node | transistor_12_out | pull_resistor_13_node | transistor_14_out | pull_resistor_15_node | transistor_16_out;  // OR_Gate or_1, 16 bits wide
  D_Flip_Flop d_ff_1 (
    .clk(\Löschen_automatisch ), .D(\Löschen_automatisch ), .Q(d_ff_1_q), .reset(d_ff_1_q));  // open: Qn, preset, en
  Shift_Register #(.width(16), .length(4)) shift_register_1 (
    .in(or_1_out), .clk(HexDiesplaySteuerung), .clr(or_2_out), .q0(shift_register_1_q0),
    .q1(shift_register_1_q1), .q2(shift_register_1_q2), .q3(shift_register_1_q3));  // open: shift, out, load, d0, d1, d2, d3
  or or_2 (or_2_out, d_ff_1_q, \Löschen_individuell );
  Shifter #(.width(16)) shifter_1 (.in(shift_register_1_q3), .\dist (4'b1100), .out(shifter_1_out));
  Shifter #(.width(16)) shifter_2 (.in(shift_register_1_q2), .\dist (4'b1000), .out(shifter_2_out));
  Shifter #(.width(16)) shifter_3 (.in(shift_register_1_q1), .\dist (4'b0100), .out(shifter_3_out));
  Adder #(.width(16)) adder_1 (.a(shifter_1_out), .b(shifter_2_out), .out(adder_1_out));  // open: cin, cout
  Adder #(.width(16)) adder_2 (.a(shifter_3_out), .b(shift_register_1_q0), .out(adder_2_out));  // open: cin, cout
  Adder #(.width(16)) adder_3 (.a(adder_1_out), .b(adder_2_out), .out(out_4));  // open: cin, cout
endmodule

module Displaycontroller (
  input  \Löschen ,
  input  [15:0] Displaydaten,
  input  [3:0] Displaysteuerung,
  input  Ausgabe_Display,
  input  Ausgabe_Display_takt,
  output [15:0] out_6,
  output [15:0] out_7,
  output [15:0] out_8,
  output [15:0] out_9,
  output [15:0] out_10,
  output [15:0] out_11,
  output [15:0] out_12,
  output [15:0] out_13,
  output [15:0] out_14,
  output [15:0] out_15,
  output [15:0] out_16,
  output [15:0] out_17,
  output [15:0] out_18,
  output [15:0] out_19,
  output [15:0] out_20,
  output [15:0] out_21
);

  wire decoder_1_out0, decoder_1_out1, decoder_1_out2, decoder_1_out3, decoder_1_out4, decoder_1_out5,
       decoder_1_out6, decoder_1_out7, decoder_1_out8, decoder_1_out9, decoder_1_out10, decoder_1_out11,
       decoder_1_out12, decoder_1_out13, decoder_1_out14, decoder_1_out15, pull_resistor_1_node;
  wire [3:0] register_1_q;

  Pull_Resistor pull_resistor_1 (.node(pull_resistor_1_node));
  Transistor #(.\type ("n"), .gate("br")) transistor_1 (
    .in(Ausgabe_Display_takt), .out(pull_resistor_1_node), .gate(Ausgabe_Display));
  Register_part #(.width(16)) _0 (
    .D(Displaydaten), .en(decoder_1_out0), .Q(out_6), .clk(pull_resistor_1_node), .clr(\Löschen ));
  Register_part #(.width(16)) _1 (
    .D(Displaydaten), .en(decoder_1_out1), .Q(out_7), .clk(pull_resistor_1_node), .clr(\Löschen ));
  Register_part #(.width(16)) _2 (
    .D(Displaydaten), .en(decoder_1_out2), .Q(out_8), .clk(pull_resistor_1_node), .clr(\Löschen ));
  Register_part #(.width(16)) _3 (
    .D(Displaydaten), .en(decoder_1_out3), .Q(out_9), .clk(pull_resistor_1_node), .clr(\Löschen ));
  Register_part #(.width(16)) _4 (
    .D(Displaydaten), .en(decoder_1_out4), .Q(out_10), .clk(pull_resistor_1_node), .clr(\Löschen ));
  Register_part #(.width(16)) _5 (
    .D(Displaydaten), .en(decoder_1_out5), .Q(out_11), .clk(pull_resistor_1_node), .clr(\Löschen ));
  Register_part #(.width(16)) _6 (
    .D(Displaydaten), .en(decoder_1_out6), .Q(out_12), .clk(pull_resistor_1_node), .clr(\Löschen ));
  Register_part #(.width(4), .trigger("high")) register_1 (
    .D(Displaysteuerung), .Q(register_1_q), .clk(Ausgabe_Display));  // open: en, clr
  Register_part #(.width(16)) _7 (
    .D(Displaydaten), .en(decoder_1_out7), .Q(out_13), .clk(pull_resistor_1_node), .clr(\Löschen ));
  Decoder #(.select(4), .disabled(0), .enable("false")) decoder_1 (
    .out0(decoder_1_out0), .out1(decoder_1_out1), .out2(decoder_1_out2), .out3(decoder_1_out3),
    .out4(decoder_1_out4), .out5(decoder_1_out5), .out6(decoder_1_out6), .out7(decoder_1_out7),
    .out8(decoder_1_out8), .out9(decoder_1_out9), .out10(decoder_1_out10), .out11(decoder_1_out11),
    .out12(decoder_1_out12), .out13(decoder_1_out13), .out14(decoder_1_out14), .out15(decoder_1_out15),
    .sel(register_1_q));
  Register_part #(.width(16)) _8 (
    .D(Displaydaten), .en(decoder_1_out8), .Q(out_14), .clk(pull_resistor_1_node), .clr(\Löschen ));
  Register_part #(.width(16)) _9 (
    .D(Displaydaten), .en(decoder_1_out9), .Q(out_15), .clk(pull_resistor_1_node), .clr(\Löschen ));
  Register_part #(.width(16)) a (
    .D(Displaydaten), .en(decoder_1_out10), .Q(out_16), .clk(pull_resistor_1_node), .clr(\Löschen ));
  Register_part #(.width(16)) b (
    .D(Displaydaten), .en(decoder_1_out11), .Q(out_17), .clk(pull_resistor_1_node), .clr(\Löschen ));
  Register_part #(.width(16)) c (
    .D(Displaydaten), .en(decoder_1_out12), .Q(out_18), .clk(pull_resistor_1_node), .clr(\Löschen ));
  Register_part #(.width(16)) d (
    .D(Displaydaten), .en(decoder_1_out13), .Q(out_19), .clk(pull_resistor_1_node), .clr(\Löschen ));
  Register_part #(.width(16)) e (
    .D(Displaydaten), .en(decoder_1_out14), .Q(out_20), .clk(pull_resistor_1_node), .clr(\Löschen ));
  Register_part #(.width(16)) f (
    .D(Displaydaten), .en(decoder_1_out15), .Q(out_21), .clk(pull_resistor_1_node), .clr(\Löschen ));
endmodule
